# Fritzing sketch wiring_GPIO-Raspberry (saved by Fritzing 0.9.2b)

parts:
  Raspberry_Pi1 = Raspberry Pi B+
  U1 = Optocoupler [package=THT]
  R1 = Resistor [tolerance=±5% resistance=220 package="0402 [SMD]"]
  J1 = double row rounded female pin header, 2 pins [form="♀ (female rounded)"]

nets:
  N1: Raspberry_Pi1.GPIO4, R1.Pin_0
  GND: Raspberry_Pi1.GND, U1.Pin_2
  N2: U1.Pin_1, R1.Pin_1
  N3: U1.Pin_4, J1.pin2
  N4: U1.Pin_5, J1.pin1

notes:
  <-- Connect to computer switch
