# Fritzing sketch Leonardo-RaspberryB (saved by Fritzing 0.9.2b)

parts:
  Raspberry_Pi_B_rev2 = Raspberry Pi B rev2
  Composants1 = Arduino Leonardo (Rev3b)

nets:
  N1: Raspberry_Pi_B_rev2.GPIO_2, Composants1.SDA
  N2: Raspberry_Pi_B_rev2.GPIO_3, Composants1.SCL
  GND: Raspberry_Pi_B_rev2.GND, Composants1.GND
