# Fritzing sketch wiring_RPI-Micro (saved by Fritzing 0.9.2b)

parts:
  Raspberry_Pi1 = Raspberry Pi B+
  Part4 = Arduino Micro (Rev3)

nets:
  N1: Raspberry_Pi1.GPIO2, Part4.D2/SDA
  N2: Raspberry_Pi1.GPIO3, Part4.D3/SCL
  GND: Raspberry_Pi1.GND, Part4.GND
