# Fritzing sketch wiring_RPI-Teensy30 (saved by Fritzing 0.9.2b)

parts:
  Raspberry_Pi1 = Raspberry Pi B+
  Teensy1 = Teensy 3.0

nets:
  N1: Raspberry_Pi1.GPIO2, Teensy1.A4/D18
  N2: Raspberry_Pi1.GPIO3, Teensy1.A5/D19
  GND: Raspberry_Pi1.GND, Teensy1.GND
