# Fritzing sketch wiring_RPI_B+-Leonardo (saved by Fritzing 0.9.2b)

parts:
  Raspberry_Pi1 = Raspberry Pi B+
  Part1 = Arduino Leonardo (Rev3b)

nets:
  N1: Raspberry_Pi1.GPIO2, Part1.SDA
  N2: Raspberry_Pi1.GPIO3, Part1.SCL
  GND: Raspberry_Pi1.GND, Part1.GND
