# Fritzing sketch wiring_RPI-Teensy++20 (saved by Fritzing 0.9.2b)

parts:
  Raspberry_Pi1 = Raspberry Pi B+
  Teensy++1 = Teensy++ 2.0

nets:
  N1: Raspberry_Pi1.GPIO2, Teensy++1.D1
  N2: Raspberry_Pi1.GPIO3, Teensy++1.D0
  GND: Raspberry_Pi1.GND, Teensy++1.GND
